// Logisim project Booth.circ as structural Verilog: 6 circuits, main circuit main
module main (
);

  Display_4_bit_to_7_segment display_4_bit_to_7_segment_1 ();  // open: I3, I2, I1, I0, D, E, G, F, A, B, C
endmodule

module Booth (
);

  Full_Adder_16_bit full_adder_16_bit_1 ();  // open: ControlBit, Input_Y, Input_X, Cout, Output
  Display_4_bit_to_7_segment display_4_bit_to_7_segment_1 ();  // open: I3, I2, I1, I0, D, E, G, F, A, B, C
endmodule

// Display_4_bit_7_seg
module Display_4_bit_to_7_segment (
  input  I3,
  input  I2,
  input  I1,
  input  I0,
  output D,
  output E,
  output G,
  output F,
  output A,
  output B,
  output C
);

  wire and_1_out, and_2_out, and_3_out, and_4_out, and_5_out, and_6_out, and_7_out, and_8_out, and_9_out,
       and_10_out, and_11_out, and_12_out, and_13_out, and_14_out, and_15_out, and_16_out, not_1_out,
       not_2_out, not_3_out, not_4_out;

  not not_1 (not_1_out, I3);
  not not_2 (not_2_out, I1);
  not not_3 (not_3_out, I2);
  not not_4 (not_4_out, I0);
  and and_1 (and_1_out, I0, I1, I2, I3);
  and and_2 (and_2_out, not_4_out, I1, I2, I3);
  and and_3 (and_3_out, I0, not_2_out, I2, I3);
  and and_4 (and_4_out, not_4_out, not_2_out, I2, I3);
  and and_5 (and_5_out, I0, I1, not_3_out, I3);
  and and_6 (and_6_out, not_4_out, I1, not_3_out, I3);
  and and_7 (and_7_out, I0, not_2_out, not_3_out, I3);
  and and_8 (and_8_out, not_4_out, not_2_out, not_3_out, I3);
  and and_9 (and_9_out, I0, I1, I2, not_1_out);
  and and_10 (and_10_out, not_4_out, I1, I2, not_1_out);
  and and_11 (and_11_out, I0, not_2_out, I2, not_1_out);
  and and_12 (and_12_out, not_4_out, not_2_out, I2, not_1_out);
  and and_13 (and_13_out, I0, I1, not_3_out, not_1_out);
  and and_14 (and_14_out, not_4_out, I1, not_3_out, not_1_out);
  and and_15 (and_15_out, I0, not_2_out, not_3_out, not_1_out);
  and and_16 (and_16_out, not_4_out, not_2_out, not_3_out, not_1_out);
  nor nor_1 (D, and_15_out, and_14_out, and_13_out, and_9_out, and_3_out);
  nor nor_2 (E, and_15_out, and_13_out, and_12_out, and_11_out, and_9_out, and_7_out);
  nor nor_3 (G, and_15_out, and_12_out, and_9_out, and_6_out, and_7_out, and_1_out);
  nor nor_4 (F, and_16_out, and_15_out, and_9_out, and_4_out);
  nor nor_5 (A, and_15_out, and_12_out, and_5_out, and_3_out);
  nor nor_6 (B, and_11_out, and_10_out, and_5_out, and_4_out, and_2_out, and_1_out);
  nor nor_7 (C, and_14_out, and_4_out, and_2_out, and_1_out);

  // Notes on the sheet:
  //   7-segment display
  //   F
  //   E
  //   D
  //   C
  //   B
  //   A
  //   9
  //   8
  //   7
  //   6
  //   5
  //   4
  //   3
  //   2
  //   1
  //   0
endmodule

// FA_16_bit
module Full_Adder_16_bit (
  input  ControlBit,
  input  [15:0] Input_X,
  input  [15:0] Input_Y,
  output [15:0] Output,
  output Cout
);

  wire full_adder_1_bit_1_cout, full_adder_1_bit_2_cout, full_adder_1_bit_3_cout, full_adder_1_bit_4_cout,
       full_adder_1_bit_5_cout, full_adder_1_bit_6_cout, full_adder_1_bit_7_cout, full_adder_1_bit_8_cout,
       full_adder_1_bit_9_cout, full_adder_1_bit_10_cout, full_adder_1_bit_11_cout, full_adder_1_bit_12_cout,
       full_adder_1_bit_13_cout, full_adder_1_bit_14_cout, full_adder_1_bit_15_cout, xor_1_out, xor_2_out,
       xor_3_out, xor_4_out, xor_5_out, xor_6_out, xor_7_out, xor_8_out, xor_9_out, xor_10_out, xor_11_out,
       xor_12_out, xor_13_out, xor_14_out, xor_15_out, xor_16_out;

  xor xor_1 (xor_1_out, Input_Y[0], ControlBit);
  xor xor_2 (xor_2_out, Input_Y[1], ControlBit);
  xor xor_3 (xor_3_out, Input_Y[2], ControlBit);
  xor xor_4 (xor_4_out, Input_Y[3], ControlBit);
  xor xor_5 (xor_5_out, Input_Y[4], ControlBit);
  xor xor_6 (xor_6_out, Input_Y[5], ControlBit);
  xor xor_7 (xor_7_out, Input_Y[6], ControlBit);
  xor xor_8 (xor_8_out, Input_Y[7], ControlBit);
  xor xor_9 (xor_9_out, Input_Y[8], ControlBit);
  xor xor_10 (xor_10_out, Input_Y[9], ControlBit);
  xor xor_11 (xor_11_out, Input_Y[10], ControlBit);
  xor xor_12 (xor_12_out, Input_Y[11], ControlBit);
  xor xor_13 (xor_13_out, Input_Y[12], ControlBit);
  xor xor_14 (xor_14_out, Input_Y[13], ControlBit);
  xor xor_15 (xor_15_out, Input_Y[14], ControlBit);
  xor xor_16 (xor_16_out, Input_Y[15], ControlBit);
  Full_Adder_1_bit full_adder_1_bit_1 (
    .Cin(ControlBit), .Input_A(xor_1_out), .Input_B(Input_X[0]), .S(Output[0]), .Cout(full_adder_1_bit_1_cout));
  Full_Adder_1_bit full_adder_1_bit_2 (
    .Cin(full_adder_1_bit_1_cout), .Input_A(xor_2_out), .Input_B(Input_X[1]), .S(Output[1]),
    .Cout(full_adder_1_bit_2_cout));
  Full_Adder_1_bit full_adder_1_bit_3 (
    .Cin(full_adder_1_bit_2_cout), .Input_A(xor_3_out), .Input_B(Input_X[2]), .S(Output[2]),
    .Cout(full_adder_1_bit_3_cout));
  Full_Adder_1_bit full_adder_1_bit_4 (
    .Cin(full_adder_1_bit_3_cout), .Input_A(xor_4_out), .Input_B(Input_X[3]), .S(Output[3]),
    .Cout(full_adder_1_bit_4_cout));
  Full_Adder_1_bit full_adder_1_bit_5 (
    .Cin(full_adder_1_bit_4_cout), .Input_A(xor_5_out), .Input_B(Input_X[4]), .S(Output[4]),
    .Cout(full_adder_1_bit_5_cout));
  Full_Adder_1_bit full_adder_1_bit_6 (
    .Cin(full_adder_1_bit_5_cout), .Input_A(xor_6_out), .Input_B(Input_X[5]), .S(Output[5]),
    .Cout(full_adder_1_bit_6_cout));
  Full_Adder_1_bit full_adder_1_bit_7 (
    .Cin(full_adder_1_bit_6_cout), .Input_A(xor_7_out), .Input_B(Input_X[6]), .S(Output[6]),
    .Cout(full_adder_1_bit_7_cout));
  Full_Adder_1_bit full_adder_1_bit_8 (
    .Cin(full_adder_1_bit_7_cout), .Input_A(xor_8_out), .Input_B(Input_X[7]), .S(Output[7]),
    .Cout(full_adder_1_bit_8_cout));
  Full_Adder_1_bit full_adder_1_bit_9 (
    .Cin(full_adder_1_bit_8_cout), .Input_A(xor_9_out), .Input_B(Input_X[8]), .S(Output[8]),
    .Cout(full_adder_1_bit_9_cout));
  Full_Adder_1_bit full_adder_1_bit_10 (
    .Cin(full_adder_1_bit_9_cout), .Input_A(xor_10_out), .Input_B(Input_X[9]), .S(Output[9]),
    .Cout(full_adder_1_bit_10_cout));
  Full_Adder_1_bit full_adder_1_bit_11 (
    .Cin(full_adder_1_bit_10_cout), .Input_A(xor_11_out), .Input_B(Input_X[10]), .S(Output[10]),
    .Cout(full_adder_1_bit_11_cout));
  Full_Adder_1_bit full_adder_1_bit_12 (
    .Cin(full_adder_1_bit_11_cout), .Input_A(xor_12_out), .Input_B(Input_X[11]), .S(Output[11]),
    .Cout(full_adder_1_bit_12_cout));
  Full_Adder_1_bit full_adder_1_bit_13 (
    .Cin(full_adder_1_bit_12_cout), .Input_A(xor_13_out), .Input_B(Input_X[12]), .S(Output[12]),
    .Cout(full_adder_1_bit_13_cout));
  Full_Adder_1_bit full_adder_1_bit_14 (
    .Cin(full_adder_1_bit_13_cout), .Input_A(xor_14_out), .Input_B(Input_X[13]), .S(Output[13]),
    .Cout(full_adder_1_bit_14_cout));
  Full_Adder_1_bit full_adder_1_bit_15 (
    .Cin(full_adder_1_bit_14_cout), .Input_A(xor_15_out), .Input_B(Input_X[14]), .S(Output[14]),
    .Cout(full_adder_1_bit_15_cout));
  Full_Adder_1_bit full_adder_1_bit_16 (
    .Cin(full_adder_1_bit_15_cout), .Input_A(xor_16_out), .Input_B(Input_X[15]), .S(Output[15]), .Cout(Cout));
endmodule

module Full_Adder_1_bit (
  input  Cin,
  input  Input_A,
  input  Input_B,
  output S,
  output Cout
);

  wire half_adder_1bit_1_cout, half_adder_1bit_1_sum, half_adder_1bit_2_cout;

  Half_Adder_1bit half_adder_1bit_1 (
    .A(Input_A), .B(Input_B), .Sum(half_adder_1bit_1_sum), .Cout(half_adder_1bit_1_cout));
  Half_Adder_1bit half_adder_1bit_2 (.A(Cin), .B(half_adder_1bit_1_sum), .Sum(S), .Cout(half_adder_1bit_2_cout));
  or or_1 (Cout, half_adder_1bit_2_cout, half_adder_1bit_1_cout);

  // Notes on the sheet:
  //   Cin
  //   A
  //   B
  //   S
  //   Cout
endmodule

module Half_Adder_1bit (
  input  A,
  input  B,
  output Sum,
  output Cout
);

  xor xor_1 (Sum, A, B);
  and and_1 (Cout, A, B);
endmodule
